# Fritzing sketch prototype (saved by Fritzing 0.9.6b)
breadboards: 1

parts:
  Part1 = Arduino Uno (Rev3) - ICSP
  R1 = Resistor [tolerance=±5% power=0.25 resistance=1k package=THT]
  R2 = Photocell (LDR) [package=THT]
  S1 = Pushbutton [package="[THT]"]
  S2 = Pushbutton [package="[THT]"]
  S3 = Pushbutton [package="[THT]"]
  S4 = Pushbutton [package="[THT]"]
  R4 = Resistor [tolerance=±5% power=0.25 resistance=10k package=THT]
  R5 = Resistor [tolerance=±5% power=0.25 resistance=10k package=THT]
  R6 = Resistor [tolerance=±5% power=0.25 resistance=10k package=THT]
  LED1 = RGB LED (com. cathode, rgb) [package="5 mm [THT]"]
  R7 = Resistor [tolerance=±5% power=0.25 resistance=220 package=THT]
  R8 = Resistor [tolerance=±5% power=0.25 resistance=220 package=THT]
  R9 = Resistor [tolerance=±5% power=0.25 resistance=220 package=THT]
  U1 = LCD-16X2 [package=lcd-16x2_noholes]
  R10 = Trimmer Potentiometer [maximum_resistance=10kΩ package=THT]
  C1 = Capacitor [part_number=105 package=cap-pth-small2]
  U2 = 74HC595 SMD [package="SO16 [SMD]"]
  R11 = Resistor [tolerance=±5% power=0.25 resistance=220 package=THT]
  ZS-042_RTC1 = ZS-042 RTC Module
  R12 = Resistor [tolerance=±5% power=0.25 resistance=10k package=THT]
  R13 = Temperature Sensor (Thermistor) [thermistor_type=NTC package=THT]
  R3 = Resistor [tolerance=±5% power=0.25 resistance=10k package=THT]

nets:
  N1: Part1.A0, R12.Pin_1, R13.pin_1
  N2: Part1.A1, R1.Pin_1, R2.pin_0
  N3: Part1.D9_PWM, R8.Pin_0
  N4: Part1.D10_PWM/SS, R9.Pin_0
  N5: Part1.D11_PWM/MOSI, U2.DS
  N6: Part1.D12/MISO, U2.ST_CP
  N7: Part1.D13/SCK, U2.SH_CP
  GND: Part1.GND, R1.Pin_0, R4.Pin_0, R5.Pin_0, R6.Pin_0, LED1.common_cathode, U1.VSS, U1.R_W, U1.K, R10.leg1, C1.2, U2.OE, ZS-042_RTC1.GND, R12.Pin_0, R3.Pin_0
  N8: Part1.A4/SDA, ZS-042_RTC1.SDA
  N9: Part1.A5/SCL, ZS-042_RTC1.SCL
  N10: Part1.D2, S1.Pin_3, S1.Pin_4, R3.Pin_1
  N11: Part1.D3_PWM, S2.Pin_3, S2.Pin_4, R4.Pin_1
  N12: Part1.D4, S3.Pin_3, S3.Pin_4, R5.Pin_1
  N13: Part1.D5_PWM, S4.Pin_3, S4.Pin_4, R6.Pin_1
  N14: Part1.D6_PWM, R7.Pin_0
  VCC: Part1.5V, R2.pin_1, S1.Pin_1, S1.Pin_2, S2.Pin_1, S2.Pin_2, S3.Pin_1, S3.Pin_2, S4.Pin_1, S4.Pin_2, U1.VDD, R10.leg2, C1.1, U2.VCC, ZS-042_RTC1.VCC, R13.pin_0
  N15: LED1.red_anode, R7.Pin_1
  N16: LED1.green_anode, R8.Pin_1
  N17: LED1.blue_anode, R9.Pin_1
  N18: U1.VO, R10.wiper
  N19: U1.RS, U2.Q1
  N20: U1.E, U2.Q3
  N21: U1.DB4, U2.Q4
  N22: U1.DB5, U2.Q5
  N23: U1.DB6, U2.Q6
  N24: U1.DB7, U2.Q7
  N25: U1.A, R11.Pin_1
  N26: U2.GND, R11.Pin_0
