# Fritzing sketch touchmetro_rev2 (saved by Fritzing 0.9.6b)
circuit board: 5.53344cm x 5.17767cm
breadboards: 1

parts:
  Cap = Adafruit Standalone 5-Pad Capacitive Touch Sensor Breakout - AT42QT1070 [part_number="Adafruit #1362"]
  LRD_Resistor = Resistor [tolerance=±5% resistance=1k power=0.25 package=THT]
  LRD = Photocell (LDR) [package=THT]
  R4 = Resistor [tolerance=±5% resistance=220 power=0.25 package=THT]
  C4 = Electrolytic Capacitor [capacitance=0.1mF voltage=50V package="100 mil [THT, electrolytic]"]
  Metro_Mini = Adafruit Metro Mini [part_number="Adafruit #2590"]
  USB = Adafruit USB Type C Breakout [part_number=4090]
  J1 = female pin header, 2 pins [form="♀ (female)"]
  J2 = female pin header, 2 pins [form="♀ (female)"]
  NEOPIXEL1 = Neopixel Strip -- White (30/m) [part_number=1376]
  DS3231 = Adafruit DS3231 [part_number="Adafruit #3013"]

nets:
  VDD: Cap.VDD, LRD.pin_0, Metro_Mini.+5V, DS3231.Vin
  N1: Cap.OUT1, Metro_Mini.IO4
  N2: Cap.OUT2, Metro_Mini.IO3
  N3: Cap.OUT3, Metro_Mini.IO2
  N4: Cap.OUT4, Metro_Mini.IO0
  N5: Cap.CAP4, J1.pin1
  N6: Cap.CAP3, J1.pin2
  N7: Cap.CAP2, J2.pin1
  N8: Cap.CAP1, J2.pin2
  GND: Cap.GND, LRD_Resistor.Pin_0, C4.-, Metro_Mini.GND, USB.GND, NEOPIXEL1.GND, DS3231.GND
  N9: LRD_Resistor.Pin_1, LRD.pin_1, Metro_Mini.AD0
  N10: R4.Pin_0, NEOPIXEL1.Din
  N11: R4.Pin_1, Metro_Mini.IO5
  VIN: C4.+, Metro_Mini.VIN, USB.VBUS, NEOPIXEL1.+5V
  N12: Metro_Mini.AD5/SCL, DS3231.SCL
  N13: Metro_Mini.AD4/SDA, DS3231.SDA

custom parts:
  Adafruit Standalone 5-Pad Capacitive Touch Sensor Breakout - AT42QT1070: This breakout board is the simplest way to create a project with mutiple capacitive touch sensors. No microcontroller is required here - just power with 1.8 to 5.5VDC and connect up to 5 conductive pads to the 5 left-hand pins. When a capacitive load is detected (e.g. a person touches one of the conductive contacts) the corresponding LED on the right lights up and the output pin goes low. You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
  Adafruit Metro Mini: We sure love the ATmega328 here at Adafruit, and we use them a lot for our own projects. The processor has plenty of GPIO, Analog inputs, hardware UART SPI and I2C, timers and PWM galore - just enough for most simple projects. When we need to go small, we use a Pro Trinket 3V or 5V, but if you want to have USB-to-Serial built in, we reach for an Adafruit METRO Mini. METRO Mini is the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
  Adafruit USB Type C Breakout: Adafruit breakout board for USB Type C socket.
  Neopixel Strip -- White (30/m): These NeoPixel strips have 30 digitally-addressable pixel LEDs per meter and are very affordable and are only 12.5 mm wide, 10 mm if you remove the strip from the casing.
  Adafruit DS3231: The datasheet for the DS3231 explains that this part is an "Extremely Accurate I²C-Integrated RTC/TCXO/Crystal". And, hey, it does exactly what it says on the tin! This Real Time Clock (RTC) is the most precise you can get in a small, low power package. Most RTCs use an external 32kHz timing crystal that is used to keep time with low current draw. And that's all well and good, but those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
